# Fritzing sketch NodeMCU-ws2813 (saved by Fritzing 0.9.3b)
breadboards: 1

parts:
  U3 = NodeMCU V1.0
  R1 = Resistor [tolerance=±5% resistance=220 package="2010 [SMD]"]
  RGB_SMD_LED1 = SMD RGB LED (WS2812) [package=5050]  # not connected

nets:
  N1: U3.D4, R1.Pin_0
  N2: U3.3V3, R1.Pin_1

custom parts:
  NodeMCU V1.0: ESP8266 based NodeMCU
